# Fritzing sketch Arduino to Processing (saved by Fritzing 0.9.1b)
breadboards: 1

parts:
  U1 = POT_SWITCH [package=pot_pth_switch]
  U2 = POT_SWITCH [package=pot_pth_switch]
  U3 = POT_SWITCH [package=pot_pth_switch]
  R1 = PHOTOCELL [package=photocell-kit]
  R2 = PHOTOCELL [package=photocell-kit]
  R3 = Resistor [tolerance=±5% resistance=220 package=THT]
  R4 = Resistor [tolerance=±5% resistance=220 package=THT]
  Parte1 = Arduino Uno (Rev3)

nets:
  N1: U1.G$1_A, U2.G$1_A, U3.G$1_A, R1.P$2, R2.P$2, Parte1.GND
  N2: U1.G$2_1, Parte1.A0
  N3: U1.G$2_2, U2.G$2_2, U3.G$2_2, R3.Pin_0, R4.Pin_0, Parte1.5V
  N4: U1.G$1_S, U1.G$1_E, U2.G$1_S, U2.G$1_E, U3.G$1_S, U3.G$1_E
  N5: U2.G$2_1, Parte1.A1
  N6: U3.G$2_1, Parte1.A2
  N7: R1.P$1, R3.Pin_1, Parte1.A3
  N8: R2.P$1, R4.Pin_1, Parte1.A4/SDA
